# Fritzing sketch WallPOWAH (saved by Fritzing 0.8.3b)
circuit board: 3.68213cm x 5.33291cm
breadboards: 1

parts:
  JR = FTDI_BASIC [package=ftdi_basic]
  JL = FTDI_BASIC [package=ftdi_basic]
  C1 = Capacitor Polarized [package=eia7343]
  POWER = Power Jack [package=power_jack_pth_lock]
  ON/OFF = SPST Switch [package=switch-spdt_lock.007s]
  Fid3 = Pad [width=2.54 height=2.54 connect=center]  # not connected
  Fid2 = Pad [width=2.54 height=2.54 connect=center]  # not connected
  Fid1 = Pad [width=2.54 height=2.54 connect=center]  # not connected

nets:
  N1: JR.5, JL.5, C1.-, POWER.GND, POWER.GNDBREAK
  N2: JR.1, JR.6, JL.6, ON/OFF.O
  N3: JR.3, JL.3
  N4: JR.4, JL.4
  N5: C1.+, POWER.PWR, ON/OFF.P

notes:
  5V GND TX  RX    VOUT
  5V GND TX  RX
  LEDgoes Wall POWAH
